# Fritzing sketch dome_circuit_design (saved by Fritzing 1.0.5)
circuit board: 8.46667cm x 5.64444cm
breadboards: 1

parts:
  RGB_SMD_LED1 = SMD RGB LED (WS2812) [package=5050]
  RGB_SMD_LED2 = SMD RGB LED (WS2812) [package=5050]
  RGB_SMD_LED3 = SMD RGB LED (WS2812) [package=5050]
  RGB_SMD_LED4 = SMD RGB LED (WS2812) [package=5050]
  HC-SR04_Sensor_1 = HC-SR04 Ultrasonic Distance Sensor
  Mod1 = Raspberry Pi 4B
  R1 = Resistor [tolerance=±5% power=0.25W resistance=1k package=THT]
  R2 = Resistor [tolerance=±5% power=0.25W resistance=1k package=THT]

nets:
  GND: RGB_SMD_LED1.DOut, RGB_SMD_LED2.DOut, HC-SR04_Sensor_1.GND, Mod1.GND, R1.Pin_1
  N1: RGB_SMD_LED1.DIn, RGB_SMD_LED4.VDD
  VCC: RGB_SMD_LED1.VCC, HC-SR04_Sensor_1.VCC, Mod1.5V
  N2: RGB_SMD_LED1.NC, RGB_SMD_LED3.VCC
  N3: RGB_SMD_LED1.VDD, RGB_SMD_LED3.DIn
  N4: RGB_SMD_LED1.VSS, RGB_SMD_LED3.DOut
  N5: RGB_SMD_LED2.DIn, Mod1.GPIO18
  VCC_2: RGB_SMD_LED2.VCC, Mod1.3V3
  N6: RGB_SMD_LED2.NC, RGB_SMD_LED4.VCC
  N7: RGB_SMD_LED2.VDD, RGB_SMD_LED4.DIn
  N8: RGB_SMD_LED2.VSS, RGB_SMD_LED4.DOut
  N9: HC-SR04_Sensor_1.TRIG, Mod1.GPIO23
  N10: HC-SR04_Sensor_1.ECHO, R2.Pin_0
  N11: Mod1.GPIO24, R1.Pin_0, R2.Pin_1
